# Fritzing sketch Sensorhub (saved by Fritzing 0.8.5b)
breadboards: 1

parts:
  Part1 = Arduino Pro Mini v13
  TRS1 = Audio Jack (TRS) 3.5mm [package="PG203J [THT]"]
  TRS2 = Audio Jack (TRS) 3.5mm [package="PG203J [THT]"]
  LED1 = LED - 5mm [color="Red (633nm)" package="5 mm [THT]"]
  LED2 = LED - 5mm [color="Green (565nm)" package="5 mm [THT]"]
  R1 = Resistor [tolerance=±5% resistance=220 package=THT]
  R2 = Resistor [tolerance=±5% resistance=220 package=THT]
  DHT-22 = Humidity and Temperature Sensor RHT03
  HC-005_Bluetooth = Bluetooth Mate Silver

nets:
  GND: Part1.GND, TRS1.Ring, TRS2.Ring, LED1.cathode, LED2.cathode, DHT-22.GND_2, HC-005_Bluetooth.GND
  5V: Part1.VCC, TRS1.Sleeve, TRS2.Sleeve, DHT-22.Vcc, HC-005_Bluetooth.VCC
  N1: Part1.D11_PWM/MOSI, HC-005_Bluetooth.RX_5V
  N2: Part1.D10_PWM/SS, HC-005_Bluetooth.TX_5V
  N3: Part1.D9_PWM, TRS2.Tip
  N4: Part1.D8, TRS1.Tip, DHT-22.Data-signal
  N5: Part1.D7, R1.Pin_1
  N6: Part1.D6_PWM, R2.Pin_1
  N7: LED1.anode, R1.Pin_0
  N8: LED2.anode, R2.Pin_0

notes:
  The DHT-22 sensor is wired directly as an example. In my setup, I connect it via a 3.5 mm jack cable
